# Fritzing sketch Wiring_Diagram (saved by Fritzing 0.9.9b)
circuit board: 8.46667cm x 5.64444cm

parts:
  3 = SWITCH-MOMENTARY-2 [package=tactile_switch_tall]
  0 = SWITCH-MOMENTARY-2 [package=tactile_switch_tall]
  9 = SWITCH-MOMENTARY-2 [package=tactile_switch_tall]
  6 = SWITCH-MOMENTARY-2 [package=tactile_switch_tall]
  part = Rectifier Diode [part_number=. package="300 mil [THT]"]
  part_2 = Rectifier Diode [part_number=. package="300 mil [THT]"]
  part_3 = Rectifier Diode [part_number=. package="300 mil [THT]"]
  part_4 = Rectifier Diode [part_number=. package="300 mil [THT]"]
  8 = SWITCH-MOMENTARY-2 [package=tactile_switch_tall]
  2 = SWITCH-MOMENTARY-2 [package=tactile_switch_tall]
  5 = SWITCH-MOMENTARY-2 [package=tactile_switch_tall]
  * = SWITCH-MOMENTARY-2 [package=tactile_switch_tall]
  part_5 = Rectifier Diode [part_number=. package="300 mil [THT]"]
  part_6 = Rectifier Diode [part_number=. package="300 mil [THT]"]
  part_7 = Rectifier Diode [part_number=. package="300 mil [THT]"]
  part_8 = Rectifier Diode [part_number=. package="300 mil [THT]"]
  7 = SWITCH-MOMENTARY-2 [package=tactile_switch_tall]
  1 = SWITCH-MOMENTARY-2 [package=tactile_switch_tall]
  4 = SWITCH-MOMENTARY-2 [package=tactile_switch_tall]
  part_9 = Rectifier Diode [part_number=. package="300 mil [THT]"]
  part_10 = Rectifier Diode [part_number=1N4148 package="300 mil [THT]"]
  part_11 = Rectifier Diode [part_number=. package="300 mil [THT]"]
  part_12 = KY-040 Rotary encoder [package=THT]
  part_13 = Arduino Pro Micro (Clone)
  R2 = Resistor [tolerance=±5% power=0.25 resistance=120 package=THT]
  R3 = Resistor [tolerance=±5% power=0.25 resistance=150 package=THT]
  R1 = Resistor [tolerance=±5% power=0.25 resistance=100 package=THT]
  LED1 = RGB LED (com. cathode, rgb) [package="5 mm [THT]"]

nets:
  N1: 3.2, 0.2, 9.2, 6.2, part_13.D16
  N2: 3.1, part_3.anode
  N3: 0.1, part.anode
  N4: 9.1, part_2.anode
  N5: 6.1, part_4.anode
  N6: part.cathode, part_8.cathode, part_13.A0
  N7: part_2.cathode, part_5.cathode, part_11.cathode, part_13.A1
  N8: part_3.cathode, part_7.cathode, part_10.cathode, part_13.A3
  N9: part_4.cathode, part_6.cathode, part_9.cathode, part_13.A2
  N10: 8.2, 2.2, 5.2, *.2, part_13.D14
  N11: 8.1, part_5.anode
  N12: 2.1, part_7.anode
  N13: 5.1, part_6.anode
  N14: *.1, part_8.anode
  N15: 7.2, 1.2, 4.2, part_13.D15
  N16: 7.1, part_11.anode
  N17: 1.1, part_10.anode
  N18: 4.1, part_9.anode
  GND: part_12.GND, part_13.GND, LED1.common_cathode
  N19: part_12.Vcc, part_13.RAW
  N20: part_12.SW, part_13.D10
  N21: part_12.DT, part_13.D2
  N22: part_12.CLK, part_13.D3
  N23: part_13.D5, R3.Pin_1
  N24: part_13.D6, R2.Pin_1
  N25: part_13.D9, R1.Pin_1
  N26: R2.Pin_0, LED1.green_anode
  N27: R3.Pin_0, LED1.red_anode
  N28: R1.Pin_0, LED1.blue_anode

custom parts:
  KY-040 Rotary encoder: KY-040 Rotary Encoder with switch on breakout borad from AZ Delivery
